// Logisim project circuito completo.circ as structural Verilog: 1 circuit, main circuit main
module main (
  input  in_1,
  input  in_2,
  input  in_3,
  input  in_4,
  input  in_5,
  input  in_6,
  input  in_7,
  input  in_8,
  input  in_9,
  input  in_10,
  input  in_11,
  input  in_12,
  input  in_13,
  input  in_14,
  input  in_15,
  input  in_16,
  input  in_17,
  input  in_18,
  input  in_19,
  input  in_20,
  input  in_21,
  input  in_22,
  input  in_23,
  input  in_24,
  input  in_25,
  input  in_26,
  input  in_27,
  input  in_28,
  input  in_29,
  input  in_30,
  input  in_31,
  input  in_32,
  input  in_33,
  input  in_34,
  input  in_35,
  output out_36,
  output out_37
);

  wire and_1_out, and_2_out, and_3_out, and_4_out, and_5_out, and_6_out, and_7_out, and_8_out, and_9_out,
       and_10_out, not_1_out, not_2_out, not_3_out, not_4_out, not_5_out, not_6_out, not_7_out, not_8_out,
       not_9_out, not_10_out, not_11_out, or_1_out, or_2_out, or_4_out, or_5_out, or_6_out, or_7_out,
       or_8_out, xor_1_out, xor_2_out, xor_3_out, xor_4_out, xor_5_out, xor_6_out, xor_7_out, xor_8_out,
       xor_9_out;

  not not_1 (not_1_out, in_5);
  not not_2 (not_2_out, in_20);
  not not_3 (not_3_out, in_32);
  not not_4 (not_4_out, in_31);
  not not_5 (not_5_out, in_7);
  not not_6 (not_6_out, in_22);
  xor xor_1 (xor_1_out, in_6, in_8);
  xor xor_2 (xor_2_out, in_6, in_7);
  and and_1 (and_1_out, not_1_out, xor_1_out, not_5_out);
  and and_2 (and_2_out, in_5, xor_2_out, in_8);
  and and_3 (and_3_out, in_20, in_21, in_22);
  and and_4 (and_4_out, not_2_out, in_21, not_6_out, in_23);
  xor xor_3 (xor_3_out, in_34, in_33);
  or or_1 (or_1_out, and_1_out, and_2_out);
  or or_2 (or_2_out, and_3_out, and_4_out);
  and and_5 (and_5_out, xor_3_out, not_3_out, not_4_out);
  and and_6 (and_6_out, in_31, in_32, in_33);
  _7_Segment_Display #(.active("false")) u_7_segment_display_1 (
    .g(in_15), .f(in_15), .a(or_1_out), .b(in_15), .e(in_15), .d(in_15), .c(in_15), .dp(in_15));
  or or_3 (out_37, and_5_out, and_6_out);
  _7_Segment_Display u_7_segment_display_2 (
    .g(in_30), .f(in_30), .a(in_30), .b(or_2_out), .e(in_30), .d(in_30), .c(in_30), .dp(in_30));
  _7_Segment_Display u_7_segment_display_3 (
    .g(out_37), .f(in_35), .a(in_35), .b(in_35), .e(in_35), .d(in_35), .c(in_35), .dp(in_35));
  not not_7 (not_7_out, in_17);
  not not_8 (not_8_out, in_4);
  xor xor_4 (xor_4_out, in_2, in_1);
  or or_4 (or_4_out, not_8_out, in_3);
  xor xor_5 (xor_5_out, in_4, in_3);
  xor xor_6 (xor_6_out, in_19, in_18);
  xor xor_7 (xor_7_out, in_18, in_17);
  or or_5 (or_5_out, xor_7_out, not_7_out, in_16, in_18);
  or or_6 (or_6_out, or_4_out, xor_5_out, xor_4_out);
  or or_7 (or_7_out, xor_6_out, or_5_out);
  _7_Segment_Display #(.active("false")) u_7_segment_display_4 (
    .g(in_14), .f(in_14), .a(in_14), .b(in_14), .e(in_14), .d(in_14), .c(or_6_out), .dp(in_14));
  _7_Segment_Display #(.active("false")) u_7_segment_display_5 (
    .g(in_28), .f(in_28), .a(in_28), .b(in_28), .e(in_28), .d(or_7_out), .c(in_28), .dp(in_28));
  not not_9 (not_9_out, in_9);
  not not_10 (not_10_out, in_11);
  not not_11 (not_11_out, in_26);
  and and_7 (and_7_out, not_10_out, xor_8_out, not_9_out);
  xor xor_8 (xor_8_out, in_12, in_10);
  and and_8 (and_8_out, in_11, in_10, in_9);
  xor xor_9 (xor_9_out, in_25, in_24);
  or or_8 (or_8_out, and_7_out, and_8_out);
  and and_9 (and_9_out, xor_9_out, not_11_out);
  and and_10 (and_10_out, in_27, in_26, in_25, in_24);
  or or_9 (out_36, and_9_out, and_10_out);
  _7_Segment_Display #(.active("false")) u_7_segment_display_6 (
    .g(in_13), .f(in_13), .a(in_13), .b(in_13), .e(or_8_out), .d(in_13), .c(in_13), .dp(in_13));
  _7_Segment_Display u_7_segment_display_7 (
    .g(in_29), .f(out_36), .a(in_29), .b(in_29), .e(in_29), .d(in_29), .c(in_29), .dp(in_29));

  // Notes on the sheet:
  //   a
  //   b
  //   g
  //   c
  //   d
  //   e
  //   f
endmodule
